# Fritzing sketch BtStation_STM32 (saved by Fritzing 0.9.3b)
circuit board: 8.46667cm x 5.64444cm
breadboards: 1

parts:
  U2 = SPI_FLASH-X25XX [package=so08]
  Part1 = BluePill
  J1 = Piezo Speaker
  R6 = Resistor [tolerance=±5% resistance=220 package=THT]
  R7 = Resistor [tolerance=±5% resistance=220 package=THT]
  R8 = Resistor [tolerance=±5% resistance=220 package=THT]
  R9 = Resistor [tolerance=±5% resistance=220 package=THT]
  R10 = Resistor [tolerance=±5% resistance=220 package=THT]
  LED3 = LED - 3mm [color="Red (633nm)" package="3 mm [THT]"]
  LED4 = LED - 3mm [color="Green (555nm)" package="3 mm [THT]"]
  Part2 = RFID-RC522 [part_number=101218]
  M1 = Bluetooth HC05 SMD [package=SMD]

nets (from the breadboard view):
  N1: U2.CS, Part1.B8
  N2: U2.MISO, Part2.MISO
  N3: U2.WP, Part1.B9
  N4: U2.MOSI, Part2.MOSI
  N5: U2.SCK, Part2.SCK
  N6: U2.HOLD, U2.VCC
  N7: Part1.A1, R6.Pin_0
  GND: Part1.GND, J1.pin1, Part2.GND
  N8: Part1.3V31, M1.pin5, M1.pin7, M1.pin8, M1.pin9, M1.pin10, M1.pin12
  N9: Part1.5V, R10.Pin_1
  N10: Part1.A10, M1.pin1
  N11: Part1.A9, M1.pin2
  N12: Part1.A8, M1.pin34
  N13: Part1.B15, R9.Pin_1
  N14: Part1.B14, R7.Pin_1
  N15: Part1.B13, R8.Pin_1
  N16: Part1.B12, M1.pin32
  N17: J1.pin2, R9.Pin_0
  N18: R6.Pin_1, LED3.cathode, LED4.cathode, M1.pin13, M1.pin21
  N19: R7.Pin_0, LED4.anode
  N20: R8.Pin_0, LED3.anode
  N21: M1.pin23, M1.pin25, M1.pin26, M1.pin27, M1.pin28, M1.pin30

custom parts:
  Bluetooth HC05 SMD: Serial port Bluetooth module (Master/Slave) HC05 bare SMD board.
